# Fritzing sketch yafg-sketch (saved by Fritzing 0.9.3b)

parts:
  Bauteil4 = Arduino Nano (Rev3.0)
  S2 = Pushbutton [package="[THT]"]
  S5 = Pushbutton [package="[THT]"]
  S6 = Pushbutton [package="[THT]"]
  S7 = Pushbutton [package="[THT]"]
  S8 = Pushbutton [package="[THT]"]
  S9 = Pushbutton [package="[THT]"]
  M2 = Stepper Motor - Bipolar
  M3 = Stepper Motor - Bipolar
  DRV_1 = DRV 8825 Stepper Motor Carrier, High Current [part_number="DRV 8825"]
  DRV_2 = DRV 8825 Stepper Motor Carrier, High Current [part_number="DRV 8825"]
  DRV_3 = DRV 8825 Stepper Motor Carrier, High Current [part_number="DRV 8825"]
  M4 = Stepper Motor - Bipolar
  R2 = Rotary Potentiometer (Small) [maximum_resistance=2kΩ package=THT]
  R1 = Resistor [tolerance=±5% resistance=1k package=THT]

nets:
  N1: Bauteil4.D2, DRV_1.DIRECTION
  N2: Bauteil4.D3, DRV_2.DIRECTION
  N3: Bauteil4.D4, DRV_3.DIRECTION
  N4: Bauteil4.D6, DRV_1.SLEEP
  N5: Bauteil4.D9, DRV_2.STEP
  N6: Bauteil4.D11/MOSI, DRV_3.STEP
  N7: Bauteil4.GND, R2.leg1, R1.Pin_1
  N8: Bauteil4.5V, R2.leg2
  N9: Bauteil4.A7, R2.wiper
  N10: Bauteil4.A5, S8.Pin_1, S8.Pin_2
  N11: Bauteil4.A4, S9.Pin_2
  N12: Bauteil4.A3, S6.Pin_1, S6.Pin_2
  N13: Bauteil4.A2, S7.Pin_2
  N14: Bauteil4.A1, S2.Pin_1, S2.Pin_2
  N15: Bauteil4.A0, S5.Pin_2
  N16: S2.Pin_3, S2.Pin_4, S5.Pin_3, S5.Pin_4, S6.Pin_3, S6.Pin_4, S7.Pin_3, S7.Pin_4, S8.Pin_3, S8.Pin_4, S9.Pin_3, S9.Pin_4, R1.Pin_0
  N17: M2.A, DRV_2.OUT_2B
  N18: M2.C, DRV_2.OUT_2A
  N19: M2.B, DRV_2.OUT_1A
  N20: M2.D, DRV_2.OUT_1B
  N21: M3.A, DRV_3.OUT_2B
  N22: M3.C, DRV_3.OUT_2A
  N23: M3.B, DRV_3.OUT_1A
  N24: M3.D, DRV_3.OUT_1B
  N25: DRV_1.OUT_2B, M4.A
  N26: DRV_1.OUT_2A, M4.C
  N27: DRV_1.OUT_1A, M4.B
  N28: DRV_1.OUT_1B, M4.D
